# Fritzing sketch hardware_setup (saved by Fritzing 0.9.3b)
breadboards: 1

parts:
  U1 = NodeMCU V3.0
  LED1 = LEDs [package=led10mm]
  Onderdeel1 = Barometric Pressure Sensor - BMP180 Breakout (GY-68)
  RHT1 = Humidity and Temperature Sensor RHT03

nets:
  N1: U1.D1, Onderdeel1.SCL
  N2: U1.D2, Onderdeel1.SDA
  N3: U1.D4, RHT1.Data-signal
  VCC: U1.3V3, Onderdeel1.VCC, RHT1.Vcc
  N4: U1.GND#6, U1.GND#13, U1.GND#16, U1.GND#33, LED1.C, Onderdeel1.GND, RHT1.GND_2
  N5: U1.D7, LED1.A

notes:
  IR Remote Control with sensors

custom parts:
  NodeMCU V3.0: ESP8266 based NodeMCU
